// Digital circuit control_unit_full.dig as structural Verilog
module control_unit_full (
  input  [5:0] opcode,
  input  [5:0] \function ,
  output jump,
  output [1:0] Branch,
  output MemRead,
  output MemWrite,
  output [1:0] MemToReg,
  output ALUSrc,
  output RegWrite,
  output RegDst,
  output InvOpcode,
  output [2:0] ALUFunc,
  output ImmExtend
);

  wire [5:0] multiplexer_1_out;
  wire [6:6] or_1_out;

  or or_1 (or_1_out[6], opcode[0], opcode[1], opcode[2], opcode[3], opcode[4], opcode[5]);
  Multiplexer #(.Bits(6)) multiplexer_1 (.sel(or_1_out[6]), .in_0(\function ), .in_1(opcode), .out(multiplexer_1_out));
  ROM #(.AddrBits(7), .Bits(15)) Control_Unit (
    .A({or_1_out[6], multiplexer_1_out}), .sel(1'b1),
    .D({ImmExtend, ALUFunc, InvOpcode, RegDst, RegWrite, ALUSrc, MemToReg, MemWrite, MemRead, Branch, jump}));

  // Notes on the sheet:
  //   contents of Control_Unit (hex, n*v repeats v):
  //   4400,4400,4400,4400,4400,4400,4400,4400,4400,4400,4400,4400,4400,4400,4400,4400,4400,
  //   4400,4400,4400,4400,4400,4400,4400,4400,4400,4400,4400,4400,4400,4400,4400,4300,4400,
  //   4b00,4400,5b00,6300,4400,4400,4400,4400,5300,4400,4400,4400,4400,4400,4400,4400,4400,
  //   4400,4400,4400,4400,4400,4400,4400,4400,4400,4400,4400,4400,4400,4400,4400,4001,4400,
  //   4802,4804,4400,4400,4180,4400,4400,4400,1980,2180,4400,4140,4400,4400,4400,4400,4400,
  //   4400,4400,4400,4400,4400,4400,4400,4400,4400,4400,4400,4400,4400,4400,41a8,4400,4400,
  //   4400,4400,4400,4400,4400,4090,4400,4400,4400,4400,4400,4400,4400,4400,4400,4400,4400,
  //   4400,4400,4400,4400,4400,4400,4400,4400,4400
endmodule
